# Fritzing sketch VolumeController (saved by Fritzing 0.9.3b)
breadboards: 1

parts:
  Part3 = TFT 1.8 inch 160x128 w microSD [part_number=358]
  Part4 = Arduino Mega 2560 (Rev3)
  ENCODER1 = Rotary Encoder with Knob
  ENCODER2 = Rotary Encoder with Knob
  ENCODER3 = Rotary Encoder with Knob
  ENCODER4 = Rotary Encoder with Knob

nets:
  N1: Part3.MOSI, Part4.D9_PWM
  N2: Part3.TFTCS, Part4.D10_PWM
  N3: Part3.CARDCS, Part4.D11_PWM
  N4: Part3.TFTDC, Part4.D12_PWM
  N5: Part3.RESET, Part4.D13_PWM
  +5V: Part3.+5V, Part4.5V, ENCODER1.no_name_yet#5, ENCODER2.no_name_yet#5, ENCODER3.no_name_yet#5, ENCODER4.no_name_yet#5
  GND: Part3.GND, Part4.GND, ENCODER1.no_name_yet#4, ENCODER2.no_name_yet#4, ENCODER3.no_name_yet#4, ENCODER4.no_name_yet#4
  N6: Part4.D22, ENCODER1.no_name_yet#1
  N7: Part4.D24, ENCODER1.no_name_yet#2
  N8: Part4.D26, ENCODER1.no_name_yet#3
  N9: Part4.D28, ENCODER2.no_name_yet#1
  N10: Part4.D30, ENCODER2.no_name_yet#2
  N11: Part4.D32, ENCODER2.no_name_yet#3
  N12: Part4.D34, ENCODER3.no_name_yet#1
  N13: Part4.D36, ENCODER3.no_name_yet#2
  N14: Part4.D38, ENCODER3.no_name_yet#3
  N15: Part4.D40, ENCODER4.no_name_yet#1
  N16: Part4.D42, ENCODER4.no_name_yet#2
  N17: Part4.D44, ENCODER4.no_name_yet#3

custom parts:
  TFT 1.8 inch 160x128 w microSD: This lovely little display breakout is the best way to add a small, colorful and bright display to any project. Since the display uses 4-wire SPI to communicate and has its own pixel-addressable frame buffer, it can be used with every kind of microcontroller. Even a very small one with low memory and few pins available! The 1.8" display has 128x160 color pixels.
  Rotary Encoder with Knob: Rotary Encoder with 1/4" Shaft and Knob
